# Fritzing sketch phoneCodeOscillatorTrinketPro (saved by Fritzing 0.9.2b)
circuit board: 3.37521cm x 3.10714cm
breadboards: 1

parts:
  C1 = Ceramic Capacitor [capacitance=10µF package="100 mil [THT, multilayer]"]
  VolumeAttenuator = Trimmer Potentiometer [maximum_resistance=10kΩ package=THT]
  C2 = Ceramic Capacitor [capacitance=0.1µF package="100 mil [THT, multilayer]"]
  R2 = Resistor [tolerance=±5% resistance=68 package=THT]
  KeyInputJack = Audio Jack (TRS) 3.5mm [package="4Ucon 08780 [THT]"]
  PowerSwitch = Toggle Switch [package=THT]
  SignalOutputJack = TRRS 3.5mm Jack Breakout
  Part3 = Pro Trinket 3.3V
  MonitorBuzzer = Piezo Speaker

nets:
  N1: C1.0, VolumeAttenuator.wiper
  N2: C1.1, SignalOutputJack.TIP, MonitorBuzzer.pin2
  N3: VolumeAttenuator.leg1, C2.0, R2.Pin_1
  N4: VolumeAttenuator.leg2, C2.1, KeyInputJack.Sleeve, SignalOutputJack.SLEEVE, Part3.RESET, MonitorBuzzer.pin1
  N5: PowerSwitch.COM, Part3.+3V3

custom parts:
  Pro Trinket 3.3V: The Pro Trinket 3.3V is like an Arduino Pro Mini with more pins and USB included. However, it uses 3V logic and 12MHz clock which means it's good when you want a lower-power and lower-voltage setup. Built with the common core Arduino chip, the ATmega328p, it has 18 GPIO, 2 extra analog inputs, 28K of flash, and 2K of RAM. It has onboard USB bootloading support with Optiboot support, so you can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
